# Fritzing sketch dht22-with-lcd (saved by Fritzing 0.9.6b)
breadboards: 1

parts:
  LCD1 = LCD screen
  Componente1 = Arduino Uno (Rev3)
  R1 = Rotary Potentiometer (Large) [maximum_resistance=100kΩ package=THT]
  R2 = Resistor [tolerance=±5% resistance=220 package="0805 [SMD]"]
  A1 = DHT22 module

nets:
  VSS: LCD1.VSS, LCD1.LED-, Componente1.GND, R1.leg1, A1.-
  VDD: LCD1.VDD, Componente1.5V, R1.leg2, R2.Pin_1, A1.+
  N1: LCD1.V0, R1.wiper
  N2: LCD1.RS, Componente1.D12/MISO
  N3: LCD1.E, Componente1.D11_PWM/MOSI
  N4: LCD1.DB4, Componente1.D5_PWM
  N5: LCD1.DB5, Componente1.D4
  N6: LCD1.DB6, Componente1.D3_PWM
  N7: LCD1.DB7, Componente1.D2
  N8: LCD1.LED+, R2.Pin_0
  N9: Componente1.D8, A1.Out

custom parts:
  DHT22 module: DHT22 module. Pins VCC Data GND.
